# Fritzing sketch Scheme (saved by Fritzing 0.9.3b)
breadboards: 1

parts:
  Part1 = Arduino Nano (Rev3.0)
  Part3 = InvenSense MPU6050
  LCD2 = LCD screen
  LCM1602_IIC2 = LCM1602 IIC [part_number="LCM1602 IIC" chip_label="LCM1602 IIC" package="DIP (Dual Inline) [THT]"]
  R1 = Resistor [tolerance=±5% resistance=4.7k package="2512 [SMD]"]
  R2 = Resistor [tolerance=±5% resistance=4.7k package="2512 [SMD]"]

nets:
  GND: Part1.GND, Part3.GND, LCM1602_IIC2.GND
  VCC: Part1.5V, Part3.VCC, LCM1602_IIC2.VCC, R1.Pin_0, R2.Pin_0
  N1: Part1.A5, Part3.SCL, LCM1602_IIC2.SCL, R2.Pin_1
  N2: Part1.A4, R1.Pin_1
  N3: Part3.SDA, LCM1602_IIC2.SDA
  VSS: LCD2.VSS, LCM1602_IIC2.VSS
  VDD: LCD2.VDD, LCM1602_IIC2.VDD
  N4: LCD2.V0, LCM1602_IIC2.V0
  N5: LCD2.RS, LCM1602_IIC2.RS
  N6: LCD2.R/W, LCM1602_IIC2.RW
  N7: LCD2.E, LCM1602_IIC2.E
  N8: LCD2.DB0, LCM1602_IIC2.D0
  N9: LCD2.DB1, LCM1602_IIC2.D1
  N10: LCD2.DB2, LCM1602_IIC2.D2
  N11: LCD2.DB3, LCM1602_IIC2.D3
  N12: LCD2.DB4, LCM1602_IIC2.D4
  N13: LCD2.DB5, LCM1602_IIC2.D5
  N14: LCD2.DB6, LCM1602_IIC2.D6
  N15: LCD2.DB7, LCM1602_IIC2.D7
  N16: LCD2.LED+, LCM1602_IIC2.A
  N17: LCD2.LED-, LCM1602_IIC2.K
  N18: LCM1602_IIC2.LED_A, LCM1602_IIC2.LED_B

custom parts:
  LCM1602 IIC: I2C-Module to use a 1602 or 2004 LCD on with the wire.h libory Serial LCD Modul
